# Fritzing sketch prototype_BME280_GP2Y1010AU0F (saved by Fritzing 0.9.4)
breadboards: 1

parts:
  WeMos_D1_Mini1 = WeMos D1 Mini
  M1 = BME280
  U1 = Sharp Dust Sensor [part_number=GP2Y1010AU0F]
  C1 = Electrolytic Capacitor [capacitance=0.22mF voltage=16V package="0605 [SMD, electrolytic]"]
  R1 = Resistor [tolerance=±2% resistance=150 package=THT]

nets:
  N1: WeMos_D1_Mini1.A0, U1.Vo
  N2: WeMos_D1_Mini1.D5, U1.LED
  N3: WeMos_D1_Mini1.G, M1.GND
  N4: U1.V-LED, C1.+, R1.Pin_0
  N5: U1.LED-GND, U1.S-GND, C1.-
  N6: U1.VCC, R1.Pin_1

custom parts:
  BME280: Temperature Humidity Barometric presure Sensor
  Sharp Dust Sensor: Sharp GP2Y1010AU0F Dust Sensor
